// Logisim project labo_checksum_etu.circ as structural Verilog: 8 circuits, main circuit Add1bit
module Add1bit (
  input  a_i,
  input  b_i,
  input  c_i,
  output r_o,
  output c_o
);

  wire and_1_out, and_2_out, and_3_out, xor_1_out;

  xor xor_1 (xor_1_out, a_i, b_i);
  and and_1 (and_1_out, a_i, b_i);
  and and_2 (and_2_out, a_i, c_i);
  and and_3 (and_3_out, b_i, c_i);
  or or_1 (c_o, and_1_out, and_2_out, and_3_out);
  xor xor_2 (r_o, xor_1_out, c_i);

  // Notes on the sheet:
  //   Attention, votre version de Logisim
  //   ne contient pas de tracker. Si vous
  //   enregistrez votre projet, toutes les
  //   informations du tracker seront
  //   définitivement effacées.
endmodule

module Add4bit (
  input  c_i,
  input  [3:0] a_i,
  input  [3:0] b_i,
  output [3:0] r_o,
  output c_o
);

  wire Add1bit_0_c_o, Add1bit_1_c_o, Add1bit_2_c_o;

  Add1bit Add1bit_0 (.a_i(a_i[0]), .b_i(b_i[0]), .c_i(c_i), .r_o(r_o[0]), .c_o(Add1bit_0_c_o));
  Add1bit Add1bit_1 (.a_i(a_i[1]), .b_i(b_i[1]), .c_i(Add1bit_0_c_o), .r_o(r_o[1]), .c_o(Add1bit_1_c_o));
  Add1bit Add1bit_2 (.a_i(a_i[2]), .b_i(b_i[2]), .c_i(Add1bit_1_c_o), .r_o(r_o[2]), .c_o(Add1bit_2_c_o));
  Add1bit Add1bit_3 (.a_i(a_i[3]), .b_i(b_i[3]), .c_i(Add1bit_2_c_o), .r_o(r_o[3]), .c_o(c_o));

  // Notes on the sheet:
  //   Attention, votre version de Logisim
  //   ne contient pas de tracker. Si vous
  //   enregistrez votre projet, toutes les
  //   informations du tracker seront
  //   définitivement effacées.
endmodule

module Sub4bit (
  input  [3:0] a_i,
  input  [3:0] b_i,
  output [3:0] r_o,
  output c_o
);

  wire Add4bit_sub_c_o;
  wire [3:0] not_1_out;

  assign not_1_out = ~b_i;  // NOT_Gate not_1, 4 bits wide
  Add4bit Add4bit_sub (.c_i(1'b1), .a_i(a_i), .b_i(not_1_out), .r_o(r_o), .c_o(Add4bit_sub_c_o));
  not not_2 (c_o, Add4bit_sub_c_o);

  // Notes on the sheet:
  //   Attention, votre version de Logisim
  //   ne contient pas de tracker. Si vous
  //   enregistrez votre projet, toutes les
  //   informations du tracker seront
  //   définitivement effacées.
endmodule

module AddSub4bit (
  input  sel_i,
  input  [3:0] a_i,
  input  [3:0] b_i,
  output [3:0] r_o,
  output c_o
);

  wire [3:0] bit_extender_1_out, xor_1_out;

  assign bit_extender_1_out = {{3{sel_i}}, sel_i};  // Bit_Extender bit_extender_1
  assign xor_1_out = bit_extender_1_out ^ b_i;  // XOR_Gate xor_1, 4 bits wide
  Add4bit Add4bit_add_sub (.c_i(sel_i), .a_i(a_i), .b_i(xor_1_out), .r_o(r_o), .c_o(c_o));

  // Notes on the sheet:
  //   Attention, votre version de Logisim
  //   ne contient pas de tracker. Si vous
  //   enregistrez votre projet, toutes les
  //   informations du tracker seront
  //   définitivement effacées.
endmodule

module Add8bit (
  input  c_i,
  input  [7:0] a_i,
  input  [7:0] b_i,
  output [7:0] r_o,
  output c_o
);

  wire Add4bit_0_3_c_o;

  Add4bit Add4bit_0_3 (.c_i(c_i), .a_i(a_i[3:0]), .b_i(b_i[3:0]), .r_o(r_o[3:0]), .c_o(Add4bit_0_3_c_o));
  Add4bit Add4bit_4_7 (.c_i(Add4bit_0_3_c_o), .a_i(a_i[7:4]), .b_i(b_i[7:4]), .r_o(r_o[7:4]), .c_o(c_o));

  // Notes on the sheet:
  //   Attention, votre version de Logisim
  //   ne contient pas de tracker. Si vous
  //   enregistrez votre projet, toutes les
  //   informations du tracker seront
  //   définitivement effacées.
endmodule

module AddSub8bit (
  input  sel_i,
  input  [7:0] a_i,
  input  [7:0] b_i,
  output [7:0] r_o,
  output c_o
);

  wire [7:0] bit_extender_1_out, xor_1_out;

  assign bit_extender_1_out = {{7{sel_i}}, sel_i};  // Bit_Extender bit_extender_1
  assign xor_1_out = b_i ^ bit_extender_1_out;  // XOR_Gate xor_1, 8 bits wide
  Add8bit Add8bit_AB (.c_i(sel_i), .a_i(a_i), .b_i(xor_1_out), .r_o(r_o), .c_o(c_o));

  // Notes on the sheet:
  //   Attention, votre version de Logisim
  //   ne contient pas de tracker. Si vous
  //   enregistrez votre projet, toutes les
  //   informations du tracker seront
  //   définitivement effacées.
endmodule

module Checksum (
  input  [7:0] a_i,
  input  [7:0] b_i,
  input  [7:0] c_i,
  output [7:0] r_o
);

  wire [7:0] AddSub8bit_AB_C_r_o, AddSub8bit_AB_r_o;

  AddSub8bit AddSub8bit_AB (.sel_i(1'b0), .a_i(a_i), .b_i(b_i), .r_o(AddSub8bit_AB_r_o));  // open: c_o
  AddSub8bit AddSub8bit_AB_C (
    .sel_i(1'b0), .a_i(AddSub8bit_AB_r_o), .b_i(c_i), .r_o(AddSub8bit_AB_C_r_o));  // open: c_o
  AddSub8bit AddSub8bit_C2 (.sel_i(1'b1), .a_i({8{1'b0}}), .b_i(AddSub8bit_AB_C_r_o), .r_o(r_o));  // open: c_o

  // Notes on the sheet:
  //   Attention, votre version de Logisim
  //   ne contient pas de tracker. Si vous
  //   enregistrez votre projet, toutes les
  //   informations du tracker seront
  //   définitivement effacées.
endmodule

module VerifyIntegrity (
  input  [7:0] a_i,
  input  [7:0] b_i,
  input  [7:0] c_i,
  input  [7:0] d_i,
  output verif_checksum_o
);

  wire [7:0] AddSub8bit_ABC_D_r_o, Checksum_ABC_r_o;

  Checksum Checksum_ABC (.a_i(a_i), .b_i(b_i), .c_i(c_i), .r_o(Checksum_ABC_r_o));
  AddSub8bit AddSub8bit_ABC_D (
    .sel_i(1'b1), .a_i(Checksum_ABC_r_o), .b_i(d_i), .r_o(AddSub8bit_ABC_D_r_o));  // open: c_o
  nor nor_1 (verif_checksum_o, AddSub8bit_ABC_D_r_o[0], AddSub8bit_ABC_D_r_o[1], AddSub8bit_ABC_D_r_o[2], AddSub8bit_ABC_D_r_o[3], AddSub8bit_ABC_D_r_o[4], AddSub8bit_ABC_D_r_o[5], AddSub8bit_ABC_D_r_o[6], AddSub8bit_ABC_D_r_o[7]);

  // Notes on the sheet:
  //   Attention, votre version de Logisim
  //   ne contient pas de tracker. Si vous
  //   enregistrez votre projet, toutes les
  //   informations du tracker seront
  //   définitivement effacées.
endmodule
