// Logisim project labo_alu_etu.circ as structural Verilog: 9 circuits, main circuit ALU_MAXV
module ALU_MAXV (
  input  [3:0] a_i,
  input  [3:0] b_i,
  output [3:0] c_o,
  output erreur_o
);

  wire [5:0] opcode_i_sw6;

  DipSwitch opcode_i (
    .sw1(opcode_i_sw6[5]), .sw2(opcode_i_sw6[4]), .sw3(opcode_i_sw6[3]), .sw4(opcode_i_sw6[2]),
    .sw5(opcode_i_sw6[1]), .sw6(opcode_i_sw6[0]));  // open: sw7, sw8
  ALU_Top alu_inst (.a_i(a_i), .b_i(b_i), .op_i(opcode_i_sw6), .c_o(c_o), .erreur_o(erreur_o));

  // Notes on the sheet:
  //   Attention, votre version de Logisim
  //   ne contient pas de tracker. Si vous
  //   enregistrez votre projet, toutes les
  //   informations du tracker seront
  //   définitivement effacées.
endmodule

module ALU_Top (
  input  [3:0] a_i,
  input  [3:0] b_i,
  input  [5:0] op_i,
  output [3:0] c_o,
  output erreur_o
);

  wire addsub4bit_opcode_1_carry_o, addsub4bit_opcode_1_negative_o, addsub4bit_opcode_1_overflow_o,
       addsub4bit_opcode_1_zero_o, and_1_out, and_2_out, and_3_out, and_4_out;
  wire [3:0] addsub4bit_opcode_1_r_o, comparateur_1_cmp_o, custom_1_s_o, unite_logique_1_f_o;

  custom custom_1 (.a_i(a_i), .s_o(custom_1_s_o));
  AddSub4bit_Opcode addsub4bit_opcode_1 (
    .a_i(a_i), .b_i(b_i), .op_i(op_i[3:2]), .r_o(addsub4bit_opcode_1_r_o),
    .carry_o(addsub4bit_opcode_1_carry_o), .zero_o(addsub4bit_opcode_1_zero_o),
    .Negative_o(addsub4bit_opcode_1_negative_o), .overflow_o(addsub4bit_opcode_1_overflow_o));
  comparateur comparateur_1 (
    .Negative_i(addsub4bit_opcode_1_negative_o), .zero_i(addsub4bit_opcode_1_zero_o),
    .carry_i(addsub4bit_opcode_1_carry_o), .op_i(op_i[2:0]), .cmp_o(comparateur_1_cmp_o));
  unite_logique unite_logique_1 (.a_i(a_i), .op_i(op_i[1:0]), .b_i(b_i), .f_o(unite_logique_1_f_o));
  Multiplexer #(.select(2), .width(4), .enable("false")) multiplexer_1 (
    .in0(addsub4bit_opcode_1_r_o), .in1(comparateur_1_cmp_o), .in2(unite_logique_1_f_o), .in3(custom_1_s_o),
    .out(c_o), .sel(op_i[5:4]));
  and and_1 (and_1_out, addsub4bit_opcode_1_overflow_o, ~op_i[4], ~op_i[5]);  // AND_Gate
  and and_2 (and_2_out, op_i[0], op_i[1], op_i[2], op_i[3], op_i[4], ~op_i[5]);  // AND_Gate
  and and_3 (and_3_out, ~op_i[0], ~op_i[1], ~op_i[2], op_i[3], op_i[4], ~op_i[5]);  // AND_Gate
  and and_4 (and_4_out, ~op_i[0], ~op_i[1], ~op_i[2], ~op_i[3], op_i[4], ~op_i[5]);  // AND_Gate
  or or_1 (erreur_o, and_1_out, and_2_out, and_3_out, and_4_out);

  // Notes on the sheet:
  //   Attention, votre version de Logisim
  //   ne contient pas de tracker. Si vous
  //   enregistrez votre projet, toutes les
  //   informations du tracker seront
  //   définitivement effacées.
endmodule

module Add1bit (
  input  a_i,
  input  b_i,
  input  c_i,
  output r_o,
  output c_o
);

  wire and_1_out, and_2_out, and_3_out, xor_1_out;

  xor xor_1 (xor_1_out, a_i, b_i);
  and and_1 (and_1_out, a_i, b_i);
  and and_2 (and_2_out, a_i, c_i);
  and and_3 (and_3_out, b_i, c_i);
  or or_1 (c_o, and_1_out, and_2_out, and_3_out);
  xor xor_2 (r_o, xor_1_out, c_i);

  // Notes on the sheet:
  //   Attention, votre version de Logisim
  //   ne contient pas de tracker. Si vous
  //   enregistrez votre projet, toutes les
  //   informations du tracker seront
  //   définitivement effacées.
endmodule

module Add4bit (
  input  c_i,
  input  [3:0] a_i,
  input  [3:0] b_i,
  output [3:0] r_o,
  output c_o
);

  wire Add1bit_0_c_o, Add1bit_1_c_o, Add1bit_2_c_o;

  Add1bit Add1bit_0 (.a_i(a_i[0]), .b_i(b_i[0]), .c_i(c_i), .r_o(r_o[0]), .c_o(Add1bit_0_c_o));
  Add1bit Add1bit_1 (.a_i(a_i[1]), .b_i(b_i[1]), .c_i(Add1bit_0_c_o), .r_o(r_o[1]), .c_o(Add1bit_1_c_o));
  Add1bit Add1bit_2 (.a_i(a_i[2]), .b_i(b_i[2]), .c_i(Add1bit_1_c_o), .r_o(r_o[2]), .c_o(Add1bit_2_c_o));
  Add1bit Add1bit_3 (.a_i(a_i[3]), .b_i(b_i[3]), .c_i(Add1bit_2_c_o), .r_o(r_o[3]), .c_o(c_o));

  // Notes on the sheet:
  //   Attention, votre version de Logisim
  //   ne contient pas de tracker. Si vous
  //   enregistrez votre projet, toutes les
  //   informations du tracker seront
  //   définitivement effacées.
endmodule

module AddSub4bit (
  input  c_i,
  input  [3:0] a_i,
  input  [3:0] b_i,
  output [3:0] r_o,
  output c_o
);

  wire [3:0] bit_extender_1_out, xor_1_out;

  assign bit_extender_1_out = {{3{c_i}}, c_i};  // Bit_Extender bit_extender_1
  assign xor_1_out = bit_extender_1_out ^ b_i;  // XOR_Gate xor_1, 4 bits wide
  Add4bit add4bit_1 (.c_i(c_i), .a_i(a_i), .b_i(xor_1_out), .r_o(r_o), .c_o(c_o));

  // Notes on the sheet:
  //   Attention, votre version de Logisim
  //   ne contient pas de tracker. Si vous
  //   enregistrez votre projet, toutes les
  //   informations du tracker seront
  //   définitivement effacées.
endmodule

module AddSub4bit_Opcode (
  input  [3:0] a_i,
  input  [3:0] b_i,
  input  [1:0] op_i,
  output [3:0] r_o,
  output carry_o,
  output zero_o,
  output Negative_o,
  output overflow_o
);

  wire and_1_out, and_2_out, and_3_out, and_4_out, and_5_out, and_6_out, and_7_out, and_8_out,
       multiplexer_1_out, or_1_out;

  // Probe on a_i
  // Probe on b_i
  and and_1 (and_1_out, ~a_i[3], r_o[3], ~b_i[3]);  // AND_Gate
  and and_2 (and_2_out, a_i[3], ~r_o[3], b_i[3]);  // AND_Gate
  and and_3 (and_3_out, ~a_i[3], r_o[3], b_i[3]);  // AND_Gate
  and and_4 (and_4_out, a_i[3], ~r_o[3], ~b_i[3]);  // AND_Gate
  AddSub4bit addsub4bit_1 (.c_i(op_i[1]), .a_i(a_i), .b_i(b_i), .r_o(r_o), .c_o(carry_o));
  and and_5 (and_5_out, a_i[3], ~r_o[3]);  // AND_Gate
  and and_6 (and_6_out, ~op_i[0], multiplexer_1_out);  // AND_Gate
  Multiplexer #(.select(2), .enable("false")) multiplexer_1 (
    .in0(and_1_out), .in1(and_2_out), .in2(and_3_out), .in3(and_4_out), .out(multiplexer_1_out),
    .sel({op_i[1], a_i[3]}));
  // Probe on r_o
  or or_1 (or_1_out, r_o[3], and_5_out);
  and and_7 (and_7_out, carry_o, ~op_i[1], op_i[0]);  // AND_Gate
  and and_8 (and_8_out, op_i[0], op_i[1], ~carry_o);  // AND_Gate
  nor nor_1 (zero_o, r_o[0], r_o[1], r_o[2], r_o[3]);
  and and_9 (Negative_o, ~op_i[0], or_1_out);  // AND_Gate
  or or_2 (overflow_o, and_7_out, and_6_out, and_8_out);

  // Notes on the sheet:
  //   Attention, votre version de Logisim
  //   ne contient pas de tracker. Si vous
  //   enregistrez votre projet, toutes les
  //   informations du tracker seront
  //   définitivement effacées.
endmodule

module comparateur (
  input  Negative_i,
  input  zero_i,
  input  carry_i,
  input  [2:0] op_i,
  output [3:0] cmp_o
);

  wire not_1_out, not_2_out, not_3_out;

  not not_1 (not_1_out, Negative_i);
  not not_2 (not_2_out, zero_i);
  not not_3 (not_3_out, carry_i);
  Multiplexer #(.select(3), .enable("false")) multiplexer_1 (
    .in0(1'b0), .in1(not_1_out), .in2(Negative_i), .in3(not_2_out), .in4(zero_i), .in5(carry_i),
    .in6(not_3_out), .in7(1'b0), .out(cmp_o[0]), .sel(op_i));

  assign cmp_o[3:1] = 3'b000;

  // Notes on the sheet:
  //   Attention, votre version de Logisim
  //   ne contient pas de tracker. Si vous
  //   enregistrez votre projet, toutes les
  //   informations du tracker seront
  //   définitivement effacées.
endmodule

module unite_logique (
  input  [3:0] a_i,
  input  [1:0] op_i,
  input  [3:0] b_i,
  output [3:0] f_o
);

  wire [3:0] and_1_out, not_1_out, or_1_out, xor_1_out;

  and and_1 (and_1_out[0], a_i[0], b_i[0]);
  and and_2 (and_1_out[1], a_i[1], b_i[1]);
  and and_3 (and_1_out[2], a_i[2], b_i[2]);
  and and_4 (and_1_out[3], a_i[3], b_i[3]);
  or or_1 (or_1_out[0], a_i[0], b_i[0]);
  or or_2 (or_1_out[1], a_i[1], b_i[1]);
  or or_3 (or_1_out[2], a_i[2], b_i[2]);
  or or_4 (or_1_out[3], a_i[3], b_i[3]);
  xor xor_1 (xor_1_out[0], a_i[0], b_i[0]);
  xor xor_2 (xor_1_out[1], a_i[1], b_i[1]);
  xor xor_3 (xor_1_out[2], a_i[2], b_i[2]);
  xor xor_4 (xor_1_out[3], a_i[3], b_i[3]);
  assign not_1_out = ~and_1_out;  // NOT_Gate not_1, 4 bits wide
  Multiplexer #(.select(2), .width(4), .enable("false")) multiplexer_1 (
    .in0(and_1_out), .in1(or_1_out), .in2(not_1_out), .in3(xor_1_out), .out(f_o), .sel(op_i));

  // Notes on the sheet:
  //   Attention, votre version de Logisim
  //   ne contient pas de tracker. Si vous
  //   enregistrez votre projet, toutes les
  //   informations du tracker seront
  //   définitivement effacées.
endmodule

module custom (
  input  [3:0] a_i,
  output [3:0] s_o
);

  wire [3:0] add4bit_1_r_o, add4bit_2_r_o;

  Add4bit add4bit_1 (.a_i({3'b000, a_i[0]}), .b_i({3'b000, a_i[1]}), .r_o(add4bit_1_r_o));  // open: c_i, c_o
  Add4bit add4bit_2 (.a_i(add4bit_1_r_o), .b_i({3'b000, a_i[2]}), .r_o(add4bit_2_r_o));  // open: c_i, c_o
  Add4bit add4bit_3 (.a_i(add4bit_2_r_o), .b_i({3'b000, a_i[3]}), .r_o(s_o));  // open: c_i, c_o

  // Notes on the sheet:
  //   Attention, votre version de Logisim
  //   ne contient pas de tracker. Si vous
  //   enregistrez votre projet, toutes les
  //   informations du tracker seront
  //   définitivement effacées.
endmodule
