// Logisim project labo_chenillard_etu.circ as structural Verilog: 5 circuits, main circuit MAXV_CHENILLARD
module MAXV_CHENILLARD (
  input  load_i,
  input  [7:0] switch_i,
  input  clk_i,
  input  nReset_i,
  output [7:0] led_o
);

  wire entree_i_sw7, entree_i_sw8, not_1_out;
  wire [1:0] entree_i_sw2;

  DipSwitch entree_i (
    .sw1(entree_i_sw2[1]), .sw2(entree_i_sw2[0]), .sw7(entree_i_sw7), .sw8(entree_i_sw8));  // open: sw3, sw4, sw5, sw6
  not not_1 (not_1_out, nReset_i);
  chenillard_TOP chenillard_TOP_1 (
    .load_i(load_i), .enable_i(entree_i_sw7), .right_nleft_i(entree_i_sw8), .speed_i(entree_i_sw2),
    .val_i(switch_i), .clk_i(clk_i), .reset_i(not_1_out), .led_o(led_o));

  // Notes on the sheet:
  //   Attention, votre version de Logisim
  //   ne contient pas de tracker. Si vous
  //   enregistrez votre projet, toutes les
  //   informations du tracker seront
  //   définitivement effacées.
endmodule

module chenillard_TOP (
  input  load_i,
  input  enable_i,
  input  right_nleft_i,
  input  [1:0] speed_i,
  input  [7:0] val_i,
  input  clk_i,
  input  reset_i,
  output [7:0] led_o
);

  wire and_1_out, done_o;
  wire [1:0] mode_i, multiplexer_2_out;
  wire [27:0] value_i;

  Multiplexer #(.select(2), .width(28), .enable("false")) multiplexer_1 (
    .in0(28'h7270e0), .in1(28'he4e1c0), .in2(28'h1c9c380), .in3(28'h3938700), .out(value_i), .sel(speed_i));
  timer_28b timer_28b_1 (
    .value_i(value_i), .load_i(load_i), .en_i(enable_i), .clk_i(clk_i), .reset_i(reset_i), .done_o(done_o));
  and and_1 (and_1_out, enable_i, done_o);
  Multiplexer #(.width(2), .enable("false")) multiplexer_2 (
    .in0(2'b00), .in1({enable_i, right_nleft_i}), .out(multiplexer_2_out), .sel(and_1_out));
  shift_reg_8b shift_reg_8b_1 (
    .value_load_i(val_i), .ser_l_i(led_o[0]), .clk_i(clk_i), .reset_i(reset_i), .mode_i(mode_i),
    .ser_r_i(led_o[7]), .val_o(led_o));
  Multiplexer #(.width(2), .enable("false")) multiplexer_3 (
    .in0(multiplexer_2_out), .in1(2'b01), .out(mode_i), .sel(load_i));

  // Other names for the same wires on the sheet: bit0 = led_o[0]; bit7 = led_o[7]

  // Notes on the sheet:
  //   Attention, votre version de Logisim
  //   ne contient pas de tracker. Si vous
  //   enregistrez votre projet, toutes les
  //   informations du tracker seront
  //   définitivement effacées.
endmodule

module shift_reg_4b (
  input  [3:0] value_load_i,
  input  ser_r_i,
  input  ser_l_i,
  input  [1:0] mode_i,
  input  clk_i,
  input  reset_i,
  output [3:0] val_o
);

  wire multiplexer_1_out, multiplexer_2_out, multiplexer_3_out, multiplexer_4_out;

  Multiplexer #(.select(2), .enable("false")) multiplexer_1 (
    .in0(val_o[3]), .in1(value_load_i[3]), .in2(val_o[2]), .in3(ser_r_i), .out(multiplexer_1_out),
    .sel(mode_i));
  D_Flip_Flop d_ff_1 (.D(multiplexer_1_out), .clk(clk_i), .Q(val_o[3]), .reset(reset_i));  // open: Qn, preset
  Multiplexer #(.select(2), .enable("false")) multiplexer_2 (
    .in0(val_o[2]), .in1(value_load_i[2]), .in2(val_o[1]), .in3(val_o[3]), .out(multiplexer_2_out),
    .sel(mode_i));
  D_Flip_Flop d_ff_2 (.D(multiplexer_2_out), .clk(clk_i), .Q(val_o[2]), .reset(reset_i));  // open: Qn, preset
  Multiplexer #(.select(2), .enable("false")) multiplexer_3 (
    .in0(val_o[1]), .in1(value_load_i[1]), .in2(val_o[0]), .in3(val_o[2]), .out(multiplexer_3_out),
    .sel(mode_i));
  D_Flip_Flop d_ff_3 (.D(multiplexer_3_out), .clk(clk_i), .Q(val_o[1]), .reset(reset_i));  // open: Qn, preset
  Multiplexer #(.select(2), .enable("false")) multiplexer_4 (
    .in0(val_o[0]), .in1(value_load_i[0]), .in2(ser_l_i), .in3(val_o[1]), .out(multiplexer_4_out),
    .sel(mode_i));
  D_Flip_Flop d_ff_4 (.D(multiplexer_4_out), .clk(clk_i), .Q(val_o[0]), .reset(reset_i));  // open: Qn, preset

  // Notes on the sheet:
  //   Attention, votre version de Logisim
  //   ne contient pas de tracker. Si vous
  //   enregistrez votre projet, toutes les
  //   informations du tracker seront
  //   définitivement effacées.
endmodule

module shift_reg_8b (
  input  [7:0] value_load_i,
  input  ser_l_i,
  input  clk_i,
  input  reset_i,
  input  [1:0] mode_i,
  input  ser_r_i,
  output [7:0] val_o
);

  shift_reg_4b shift_reg_4b_1 (
    .value_load_i(value_load_i[3:0]), .ser_r_i(val_o[4]), .ser_l_i(ser_l_i), .mode_i(mode_i), .clk_i(clk_i),
    .reset_i(reset_i), .val_o(val_o[3:0]));
  shift_reg_4b shift_reg_4b_2 (
    .value_load_i(value_load_i[7:4]), .ser_r_i(ser_r_i), .ser_l_i(val_o[3]), .mode_i(mode_i), .clk_i(clk_i),
    .reset_i(reset_i), .val_o(val_o[7:4]));

  // Notes on the sheet:
  //   Attention, votre version de Logisim
  //   ne contient pas de tracker. Si vous
  //   enregistrez votre projet, toutes les
  //   informations du tracker seront
  //   définitivement effacées.
endmodule

module timer_28b (
  input  [27:0] value_i,
  input  load_i,
  input  en_i,
  input  clk_i,
  input  reset_i,
  output done_o
);

  wire comparator_1_eq, comparator_1_lt;
  wire [27:0] adder_1_out, multiplexer_1_out, multiplexer_2_out, register_1_q;

  Multiplexer #(.width(28), .enable("false")) multiplexer_1 (
    .in0(adder_1_out), .in1({28{1'b0}}), .out(multiplexer_1_out), .sel(done_o));
  Multiplexer #(.width(28), .enable("false")) multiplexer_2 (
    .in0(multiplexer_1_out), .in1(value_i), .out(multiplexer_2_out), .sel(load_i));
  Register #(.width(28)) register_1 (.D(multiplexer_2_out), .en(en_i), .clk(clk_i), .Q(register_1_q), .clr(reset_i));
  Adder #(.width(28)) adder_1 (.a(28'h1), .b(register_1_q), .out(adder_1_out), .cin(1'b0));  // open: cout
  Comparator #(.width(28)) comparator_1 (
    .a(value_i), .b(register_1_q), .eq(comparator_1_eq), .lt(comparator_1_lt));  // open: gt
  or or_1 (done_o, comparator_1_lt, comparator_1_eq);

  // Notes on the sheet:
  //   Attention, votre version de Logisim
  //   ne contient pas de tracker. Si vous
  //   enregistrez votre projet, toutes les
  //   informations du tracker seront
  //   définitivement effacées.
endmodule
